# Fritzing sketch apcsolo (saved by Fritzing 0.9.10b)
circuit board: 5.44482cm x 4.54558cm

parts:
  556 = IC, DIP package, 14 pins [chip_label=556]
  R24 = Resistor [tolerance=±5% power=0.25 resistance=1k package=THT]
  C3 = Ceramic Capacitor [capacitance=100nF voltage=35V package="100 mil [THT, multilayer]"]
  C4 = Ceramic Capacitor [capacitance=10nF voltage=35V package="100 mil [THT, multilayer]"]
  R25 = Resistor [tolerance=±5% power=0.25 resistance=470k package=THT]
  R26 = Resistor [tolerance=±5% power=0.25 resistance=4.7k package=THT]
  audio_out = female pin header, 2 pins [form="♀ (female)"]
  R27 = Rotary Potentiometer (Large) [maximum_resistance=500kΩ knob_status=50% power=0.5W package=THT]
  R28 = Rotary Potentiometer (Large) [maximum_resistance=500kΩ knob_status=50% power=0.5W package=THT]
  gate_in = female pin header, 2 pins [form="♀ (female)"]
  power_in = female pin header, 2 pins [form="♀ (female)"]
  slct_gate = male pin header, 3 pins [form="♂ (male)"]
  C5 = Electrolytic Capacitor [capacitance=470µF voltage=35V package="100 mil [THT, electrolytic]"]  # not connected

nets:
  N1: 556.pin1, R24.Pin_1, R28.leg2, slct_gate.pin1
  N2: 556.pin2, 556.pin6, R24.Pin_0, C4.1
  9V: 556.pin4, 556.pin10, 556.pin14, R27.leg1, R27.wiper, R28.leg1, R28.wiper, power_in.pin1
  N3: 556.pin5, 556.pin8
  GND: 556.pin7, C3.0, C4.0, R26.Pin_1, audio_out.pin2, gate_in.pin2, power_in.pin2
  N4: 556.pin9, R25.Pin_0
  N5: 556.pin12, 556.pin13, C3.1, R27.leg2, slct_gate.pin3
  N6: R25.Pin_1, R26.Pin_0, audio_out.pin1
  N7: gate_in.pin1, slct_gate.pin2

notes:
  découplage !!!
