# Fritzing sketch babyStep3 (saved by Fritzing 0.9.10b)
circuit board: 19.81cm x 5.33cm

parts:
  D1 = Diode [package=diode-1n4148]
  D2 = Diode [package=diode-1n4148]
  D3 = Diode [package=diode-1n4148]
  D4 = Diode [package=diode-1n4148]
  D5 = Diode [package=diode-1n4148]
  D7 = Diode [package=diode-1n4148]
  D8 = Diode [package=diode-1n4148]
  4017 = IC, DIP package, 16 pins [chip_label=IC]
  R9 = Rotary Potentiometer (Large) [maximum_resistance=100kΩ knob_status=50% power=0.5W package=THT]
  R1 = Rotary Potentiometer (Large) [maximum_resistance=100kΩ knob_status=50% power=0.5W package=THT]
  R2 = Rotary Potentiometer (Large) [maximum_resistance=100kΩ knob_status=50% power=0.5W package=THT]
  R3 = Rotary Potentiometer (Large) [maximum_resistance=100kΩ knob_status=50% power=0.5W package=THT]
  R4 = Rotary Potentiometer (Large) [maximum_resistance=100kΩ knob_status=50% power=0.5W package=THT]
  R5 = Rotary Potentiometer (Large) [maximum_resistance=100kΩ knob_status=50% power=0.5W package=THT]
  R6 = Rotary Potentiometer (Large) [maximum_resistance=100kΩ knob_status=50% power=0.5W package=THT]
  R7 = Rotary Potentiometer (Large) [maximum_resistance=100kΩ knob_status=50% power=0.5W package=THT]
  R8 = Rotary Potentiometer (Large) [maximum_resistance=100kΩ knob_status=50% power=0.5W package=THT]
  R11 = Resistor [tolerance=±5% power=0.25 resistance=4.7k package=THT]
  LED1 = LED - 3mm [color="Red (633nm)" current=0.030 package="3 mm [THT]"]
  R12 = Resistor [tolerance=±5% power=0.25 resistance=4.7k package=THT]
  LED2 = LED - 3mm [color="Red (633nm)" current=0.030 package="3 mm [THT]"]
  R13 = Resistor [tolerance=±5% power=0.25 resistance=4.7k package=THT]
  LED3 = LED - 3mm [color="Red (633nm)" current=0.030 package="3 mm [THT]"]
  R14 = Resistor [tolerance=±5% power=0.25 resistance=4.7k package=THT]
  LED4 = LED - 3mm [color="Red (633nm)" current=0.030 package="3 mm [THT]"]
  R15 = Resistor [tolerance=±5% power=0.25 resistance=4.7k package=THT]
  LED5 = LED - 3mm [color="Red (633nm)" current=0.030 package="3 mm [THT]"]
  R16 = Resistor [tolerance=±5% power=0.25 resistance=4.7k package=THT]
  LED6 = LED - 3mm [color="Red (633nm)" current=0.030 package="3 mm [THT]"]
  R17 = Resistor [tolerance=±5% power=0.25 resistance=4.7k package=THT]
  LED7 = LED - 3mm [color="Red (633nm)" current=0.030 package="3 mm [THT]"]
  R18 = Resistor [tolerance=±5% power=0.25 resistance=4.7k package=THT]
  LED8 = LED - 3mm [color="Red (633nm)" current=0.030 package="3 mm [THT]"]
  D6 = Diode [package=diode-1n4148]
  40106 = IC, DIP package, 14 pins [chip_label=IC]
  gt_out = female pin header, 2 pins [form="♀ (female)"]
  pwr = male pin header, 2 pins [form="♂ (male)"]
  C1 = Electrolytic Capacitor [capacitance=10µF voltage=35V package="100 mil [THT, electrolytic]"]  # not connected

nets:
  N1: D1.A, R1.wiper
  N2: D1.C, D2.C, D3.C, D4.C, D5.C, D7.C, D8.C, D6.C, gt_out.pin2
  N3: D2.A, R2.wiper
  N4: D3.A, R3.wiper
  N5: D4.A, R4.wiper
  N6: D5.A, R5.wiper
  N7: D7.A, R7.wiper
  N8: D8.A, R8.wiper
  N9: 4017.pin1, R6.leg1, R16.Pin_1
  N10: 4017.pin2, R2.leg1, R12.Pin_1
  N11: 4017.pin3, R1.leg1, R11.Pin_1
  N12: 4017.pin4, R3.leg1, R13.Pin_1
  N13: 4017.pin5, R7.leg1, R17.Pin_1
  N14: 4017.pin6, R8.leg1, R18.Pin_1
  N15: 4017.pin7, R4.leg1, R14.Pin_1
  GND: 4017.pin8, 4017.pin13, R1.leg2, R2.leg2, R3.leg2, R4.leg2, R5.leg2, R6.leg2, R7.leg2, R8.leg2, LED1.cathode, LED2.cathode, LED3.cathode, LED4.cathode, LED5.cathode, LED6.cathode, LED7.cathode, LED8.cathode, 40106.pin7, gt_out.pin1, pwr.pin2
  N16: 4017.pin9, 4017.pin15
  N17: 4017.pin10, R5.leg1, R15.Pin_1
  N18: 4017.pin14, R9.leg2, 40106.pin2
  9V: 4017.pin16, 40106.pin14, pwr.pin1
  N19: R9.leg1, R9.wiper, 40106.pin1
  N20: R6.wiper, D6.A
  N21: R11.Pin_0, LED1.anode
  N22: R12.Pin_0, LED2.anode
  N23: R13.Pin_0, LED3.anode
  N24: R14.Pin_0, LED4.anode
  N25: R15.Pin_0, LED5.anode
  N26: R16.Pin_0, LED6.anode
  N27: R17.Pin_0, LED7.anode
  N28: R18.Pin_0, LED8.anode

notes:
  +
  sig
  Il manque un condo entre pin1 et GND !!!!!!
